// Logisim project ALU.circ as structural Verilog: 1 circuit, main circuit main
// ALU
module main (
  input  [31:0] BusA,
  input  [31:0] BusB,
  input  [1:0] f,
  input  [4:0] OPcode,
  output [31:0] ALUresult
);

  wire comparator_1_eq, comparator_2_lt;
  wire [3:0] ALUop;
  wire [31:0] ALUresult_4, ALUresult_5, ALUresult_6, ALUresult_7, ALUresult_8, ALUresult_9, ALUresult_10,
       ALUresult_11, ALUresult_12, ALUresult_13, ALUresult_14, ALUresult_15, negator_1_out, not_1_out;

  ROM #(.addrWidth(7), .dataWidth(4)) rom_1 (.addr({OPcode, f}), .data(ALUop));  // open: sel
  assign not_1_out = ~BusA;  // NOT_Gate not_1, 32 bits wide
  Adder #(.width(32)) adder_1 (.a(BusA), .b(BusB), .out(ALUresult_8));  // open: cin, cout
  Negator #(.width(32)) negator_1 (.in(BusA), .out(negator_1_out));
  Adder #(.width(32)) adder_2 (.a(negator_1_out), .b(BusB), .out(ALUresult_9));  // open: cin, cout
  Comparator #(.width(32)) comparator_1 (.a(BusA), .b(BusB), .eq(comparator_1_eq));  // open: gt, lt
  Comparator #(.width(32)) comparator_2 (.a(BusA), .b(BusB), .lt(comparator_2_lt));  // open: gt, eq
  Shifter #(.width(32)) shifter_1 (.in(BusA), .\dist (BusB[4:0]), .out(ALUresult_12));
  Shifter #(.width(32), .shift("lr")) shifter_2 (.in(BusA), .\dist (BusB[4:0]), .out(ALUresult_13));
  Shifter #(.width(32), .shift("ar")) shifter_3 (.in(BusA), .\dist (BusB[4:0]), .out(ALUresult_14));
  Shifter #(.width(32), .shift("rr")) shifter_4 (.in(BusA), .\dist (BusB[4:0]), .out(ALUresult_15));
  assign ALUresult_4 = BusA & BusB;  // AND_Gate ANDI, 32 bits wide
  assign ALUresult_5 = not_1_out & BusB;  // AND_Gate CANDI, 32 bits wide
  assign ALUresult_6 = BusA | BusB;  // OR_Gate ORI, 32 bits wide
  assign ALUresult_7 = BusA ^ BusB;  // XOR_Gate XOR, 32 bits wide
  assign ALUresult_10 = {{31{1'b0}}, comparator_1_eq};  // Bit_Extender bit_extender_1
  assign ALUresult_11 = {{31{1'b0}}, comparator_2_lt};  // Bit_Extender bit_extender_2
  Multiplexer #(.select(4), .width(32)) multiplexer_1 (
    .in0(ALUresult_4), .in1(ALUresult_5), .in2(ALUresult_6), .in3(ALUresult_7), .in4(ALUresult_8),
    .in5(ALUresult_9), .in6(ALUresult_10), .in7(ALUresult_11), .in8(ALUresult_12), .in9(ALUresult_13),
    .in10(ALUresult_14), .in11(ALUresult_15), .out(ALUresult), .sel(ALUop));  // open: in12, in13, in14, in15, en

  // Notes on the sheet:
  //   contents of rom_1 (hex, n*v repeats v):
  //   0 1 2 3 4 5 6 7 12*0 1 0 0 0 2 0 0 0 3 0 0 0 4 0 0 0 5 0 0 0 6 0 0 0 7 0 0 0 8 0 0 0 9 0 0 0 a 0 0 0
  //   b
endmodule
