// Logisim project CPU.circ as structural Verilog: 2 circuits, main circuit main
module main (
  input  en
);

  wire ALUSrc, Clk, ExtOp, MemRd, MemWr, RegDst, RegWr, WBdata;
  wire [1:0] f, main_1_p4;
  wire [2:0] multiplexer_1_out, Ra, Rb, Rd;
  wire [4:0] imm_5, Op;
  wire [10:0] imm_11;
  wire [15:0] rom_1_data;
  wire [19:0] adder_1_out, adder_2_out, adder_3_out, bit_extender_1_out, bit_extender_2_out,
       multiplexer_3_out, PC;
  wire [31:0] BusA, BusB, BusW, imm_5_Ext, main_3_aluresult, multiplexer_2_out, ram_1_data;

  Multiplexer #(.width(3)) multiplexer_1 (.in0(Rb), .in1(Rd), .out(multiplexer_1_out), .sel(RegDst), .en(1'b1));
  // PcSrc_main main_1: pin names not known; wires that end beside it: Op, BusA, BusB, main_1_p4
  assign bit_extender_1_out = {{15{imm_5[4]}}, imm_5};  // Bit_Extender bit_extender_1
  assign bit_extender_2_out = {{9{imm_11[10]}}, imm_11};  // Bit_Extender bit_extender_2
  Reg_File_main main_2 (
    .BusW(BusW), .RA(Ra), .RB(Rb), .RW(multiplexer_1_out), .RegWrite(RegWr), .BusA(BusA), .BusB(BusB),
    .Clk(Clk));
  Adder #(.width(20)) adder_1 (.a(PC), .b(20'h1), .out(adder_1_out));  // open: cin, cout
  Adder #(.width(20)) adder_2 (.a(PC), .b(bit_extender_1_out), .out(adder_2_out));  // open: cin, cout
  Adder #(.width(20)) adder_3 (.a(PC), .b(bit_extender_2_out), .out(adder_3_out));  // open: cin, cout
  Multiplexer #(.width(32), .enable("false")) multiplexer_2 (
    .in0(BusB), .in1(imm_5_Ext), .out(multiplexer_2_out), .sel(ALUSrc));
  Multiplexer #(.select(2), .width(20)) multiplexer_3 (
    .in0(adder_1_out), .in1(adder_2_out), .in2(adder_3_out), .in3(BusA[19:0]), .out(multiplexer_3_out),
    .sel(main_1_p4), .en(1'b1));
  ALU_main main_3 (.BusA(BusA), .BusB(multiplexer_2_out), .f(f), .OPcode(Op), .ALUresult(main_3_aluresult));
  Register #(.width(20)) register_1 (.D(multiplexer_3_out), .en(1'b1), .Q(PC), .clk(Clk), .clr(en));
  Clock u_clk (.out(Clk));
  assign imm_5_Ext = {{27{1'b0}}, imm_5};  // Bit_Extender bit_extender_3
  ROM #(.addrWidth(20), .dataWidth(16)) rom_1 (.addr(PC), .data(rom_1_data), .sel(1'b1));
  RAM #(.addrWidth(20), .dataWidth(32), .bus("separate")) ram_1 (
    .addr(main_3_aluresult[19:0]), .din(BusB), .data(ram_1_data), .str(MemWr), .sel(1'b1), .clk(Clk),
    .ld(MemRd));  // open: clr
  instruction_Decoder_main main_4 (
    .in_1(rom_1_data), .OPcode(Op), .J_imm(imm_11), .Ra(Ra), .Rb(Rb), .imm(imm_5), .Rd(Rd), .f(f));
  Multiplexer #(.width(32), .enable("false")) multiplexer_4 (
    .in0(main_3_aluresult), .in1(ram_1_data), .out(BusW), .sel(WBdata));
  Main_Control main_control_1 (
    .Op4(Op[4]), .Op3(Op[3]), .Op2(Op[2]), .Op1(Op[1]), .Op0(Op[0]), .RegDst(RegDst), .RegWr(RegWr),
    .ExtOp(ExtOp), .ALUSrc(ALUSrc), .MemRd(MemRd), .MemWr(MemWr), .WBdata(WBdata));

  // Notes on the sheet:
  //   contents of rom_1 (hex, n*v repeats v):
  //   4 c 3048 a940 200 3043 a941 200 3046 a942 200 304b a943 200 3045 a944 200 304f a945 200 3047 a946
  //   200 3049 a947 200 304d a948 200 3042 a949 200 304a e802 e010 4361 46c1 a180 a1a1 9583 a9a0 a981 4121
  //   8ad8 600 100 8a74 d8e0 e000
endmodule

module Main_Control (
  input  Op4,
  input  Op3,
  input  Op2,
  input  Op1,
  input  Op0,
  output RegDst,
  output RegWr,
  output ExtOp,
  output ALUSrc,
  output MemRd,
  output MemWr,
  output WBdata
);

  wire and_2_out, and_3_out, and_6_out, and_7_out, and_8_out, and_9_out, not_1_out, not_2_out, not_3_out,
       not_4_out, not_5_out, not_6_out, not_7_out, not_8_out, not_9_out, not_10_out, not_11_out, not_12_out,
       not_13_out, not_14_out;

  not not_1 (not_1_out, Op4);
  not not_2 (not_2_out, Op3);
  not not_3 (not_3_out, Op2);
  not not_4 (not_4_out, Op3);
  not not_5 (not_5_out, Op0);
  not not_6 (not_6_out, Op2);
  or or_1 (ExtOp, Op3, Op4);
  or or_2 (ALUSrc, Op2, Op3);
  not not_7 (not_7_out, Op3);
  not not_8 (not_8_out, Op1);
  not not_9 (not_9_out, Op0);
  not not_10 (not_10_out, Op3);
  not not_11 (not_11_out, Op1);
  not not_12 (not_12_out, Op2);
  not not_13 (not_13_out, Op0);
  and and_1 (RegDst, not_1_out, not_2_out, not_3_out);
  not not_14 (not_14_out, Op4);
  and and_2 (and_2_out, not_4_out, Op2, not_5_out);
  and and_3 (and_3_out, Op3, not_6_out);
  and and_4 (MemRd, Op4, not_7_out, Op2, not_8_out, not_9_out);
  and and_5 (MemWr, Op4, not_10_out, Op2, not_11_out, Op0);
  and and_6 (and_6_out, Op4, not_12_out);
  and and_7 (and_7_out, Op4, not_13_out);
  and and_8 (and_8_out, Op4, Op1);
  and and_9 (and_9_out, Op4, Op3);
  or or_3 (RegWr, not_14_out, and_2_out, and_3_out);
  or or_4 (WBdata, and_6_out, and_7_out, and_8_out, and_9_out);
endmodule
