// Logisim project Main_Control_Unit.circ as structural Verilog: 1 circuit, main circuit Main_Control
module Main_Control (
  input  Op4,
  input  Op3,
  input  Op2,
  input  Op1,
  input  Op0,
  output RegDst,
  output RegWr,
  output ExtOp,
  output ALUSrc,
  output MemRd,
  output MemWr,
  output WBdata
);

  wire and_2_out, and_3_out, not_1_out, not_2_out, not_3_out, not_4_out, not_5_out, not_6_out, not_7_out,
       not_8_out, not_9_out, not_10_out;

  not not_1 (not_1_out, Op4);
  not not_2 (not_2_out, Op3);
  not not_3 (not_3_out, Op2);
  not not_4 (not_4_out, Op3);
  not not_5 (not_5_out, Op0);
  not not_6 (not_6_out, Op2);
  or or_1 (ExtOp, Op3, Op4);
  or or_2 (ALUSrc, Op2, Op3);
  not not_7 (not_7_out, Op3);
  not not_8 (not_8_out, Op0);
  not not_9 (not_9_out, Op3);
  and and_1 (RegDst, not_1_out, not_2_out, not_3_out);
  not not_10 (not_10_out, Op4);
  and and_2 (and_2_out, not_4_out, Op2, not_5_out);
  and and_3 (and_3_out, Op3, not_6_out);
  and and_4 (MemRd, Op4, not_7_out, Op2, not_8_out);
  and and_5 (MemWr, Op4, not_9_out, Op2, Op0);
  or or_3 (RegWr, not_10_out, and_2_out, and_3_out);

  assign WBdata = Op4;
endmodule
