// Logisim project instruction_Decoder.circ as structural Verilog: 1 circuit, main circuit main
module main (
  input  [15:0] in_1,
  output [4:0] OPcode,
  output [10:0] J_imm,
  output [2:0] Ra,
  output [2:0] Rb,
  output [4:0] imm,
  output [2:0] Rd,
  output [1:0] f
);


  assign f = in_1[1:0];
  assign imm = in_1[4:0];
  assign J_imm = in_1[10:0];
  assign OPcode = in_1[15:11];
  assign Ra = in_1[10:8];
  assign Rb = in_1[7:5];
  assign Rd = in_1[4:2];
endmodule
